// Digital circuit Compteur16bits.dig as structural Verilog
module Compteur16bits (
  input  CLK,
  input  WE,
  input  Reset,
  output [15:0] Cmpt,
  output Cout
);

  wire add8bit2_1_c0;
  wire [7:0] add8bit2_1_s, add8bit2_2_s;

  add8bit2 add8bit2_1 (.A({8{1'b0}}), .B(Cmpt[15:8]), .S(add8bit2_1_s), .ci(1'b0), .C0(add8bit2_1_c0));
  registre8bit registre8bit_1 (.in(add8bit2_1_s), .CLK(CLK), .WE(WE), .Reset(Reset), .out(Cmpt[15:8]));
  add8bit2 add8bit2_2 (.A(8'h1), .B(Cmpt[7:0]), .S(add8bit2_2_s), .ci(add8bit2_1_c0), .C0(Cout));
  registre8bit registre8bit_2 (.in(add8bit2_2_s), .CLK(CLK), .WE(WE), .Reset(Reset), .out(Cmpt[7:0]));
endmodule
