// Digital circuit Compteur8bit.dig as structural Verilog
module Compteur8bit (
  input  CLK,
  input  WE,
  input  Reset,
  output [7:0] Cmpt,
  output cout
);

  wire [7:0] add8bit2_1_s;

  add8bit2 add8bit2_1 (.A(8'h1), .B(Cmpt), .ci(1'b0), .S(add8bit2_1_s), .C0(cout));
  registre8bit registre8bit_1 (.in(add8bit2_1_s), .CLK(CLK), .WE(WE), .Reset(Reset), .out(Cmpt));
endmodule
