// Digital circuit Compteur8bittime.dig as structural Verilog
module Compteur8bittime (
  input  CLK,
  input  WE,
  input  Reset,
  input  [7:0] Limit,
  output [7:0] Cmpt,
  output cout
);

  wire comp8bit_1_out, xor_1_out;
  wire [7:0] add8bit2_1_s;

  add8bit2 add8bit2_1 (.A(8'h1), .B(Cmpt), .ci(1'b0), .S(add8bit2_1_s), .C0(cout));
  xor xor_1 (xor_1_out, WE, comp8bit_1_out);
  registre8bit registre8bit_1 (.in(add8bit2_1_s), .CLK(CLK), .WE(xor_1_out), .Reset(Reset), .out(Cmpt));
  comp8bit comp8bit_1 (.A(Cmpt), .B(Limit), .out(comp8bit_1_out));
endmodule
