// Digital circuit D-fliflop-res1bit.dig as structural Verilog
module D_fliflop_res1bit (
  input  D,
  input  EN,
  input  CLK,
  input  Reset,
  output Q
);

  wire multiplexer_1_out, multiplexer_2_out;

  Multiplexer multiplexer_1 (.sel(Reset), .in_0(D), .in_1(1'b0), .out(multiplexer_1_out));
  Multiplexer multiplexer_2 (.sel(EN), .in_0(Q), .in_1(multiplexer_1_out), .out(multiplexer_2_out));
  D_flipflop1bit d_flipflop1bit_1 (.in(multiplexer_2_out), .clk(CLK), .out(Q));
endmodule
