// Digital circuit D-flipflop1bit.dig as structural Verilog
module D_flipflop1bit (
  input  in,
  input  clk,
  output out
);

  wire multiplexer_1_out;

  Multiplexer multiplexer_1 (.sel(clk), .in_0(in), .in_1(multiplexer_1_out), .out(multiplexer_1_out));
  Multiplexer multiplexer_2 (.sel(clk), .in_0(out), .in_1(multiplexer_1_out), .out(out));
endmodule
