// Digital circuit Dlatch1bit.dig as structural Verilog
module Dlatch1bit (
  input  in,
  input  keep,
  output out
);

  Multiplexer multiplexer_1 (.sel(keep), .in_0(in), .in_1(out), .out(out));
endmodule
