// Digital circuit add1bit.dig as structural Verilog
module add1bit (
  input  A,
  input  B,
  input  Cin,
  output S,
  output Cout
);

  wire and_1_out, and_2_out, xor_1_out;

  or or_1 (Cout, and_2_out, and_1_out);
  and and_1 (and_1_out, B, A);
  and and_2 (and_2_out, Cin, xor_1_out);
  xor xor_1 (xor_1_out, B, A);
  xor xor_2 (S, Cin, xor_1_out);
endmodule
