// Digital circuit add4bit.dig as structural Verilog
module add4bit (
  input  c0,
  input  S,
  output ci,
  output A,
  output B
);

  wire add1bit_1_s, add1bit_2_cout, add1bit_2_s, add1bit_3_cout, add1bit_3_s, add1bit_4_cout, undriven,
       undriven_2, undriven_3, undriven_4, undriven_5, undriven_6;

  add1bit add1bit_1 (.A(undriven), .B(undriven_4), .Cin(add1bit_2_cout), .S(add1bit_1_s), .Cout(c0));
  add1bit add1bit_2 (.A(undriven_2), .B(undriven_5), .Cin(add1bit_3_cout), .S(add1bit_2_s), .Cout(add1bit_2_cout));
  add1bit add1bit_3 (.A(undriven_3), .B(undriven_6), .Cin(add1bit_4_cout), .S(add1bit_3_s), .Cout(add1bit_3_cout));
  add1bit add1bit_4 (.A(A), .B(B), .Cin(ci), .S(S), .Cout(add1bit_4_cout));
endmodule
