// Digital circuit add4bit2.0.dig as structural Verilog
module add4bit2_0 (
  input  [3:0] A,
  input  [3:0] B,
  input  Ci,
  output C0,
  output [3:0] S
);

  wire add1bit_2_cout, add1bit_3_cout, add1bit_4_cout;

  add1bit add1bit_1 (.A(A[3]), .B(B[3]), .Cin(add1bit_2_cout), .S(S[3]), .Cout(C0));
  add1bit add1bit_2 (.A(A[2]), .B(B[2]), .Cin(add1bit_3_cout), .S(S[2]), .Cout(add1bit_2_cout));
  add1bit add1bit_3 (.A(A[1]), .B(B[1]), .Cin(add1bit_4_cout), .S(S[1]), .Cout(add1bit_3_cout));
  add1bit add1bit_4 (.A(A[0]), .B(B[0]), .Cin(Ci), .S(S[0]), .Cout(add1bit_4_cout));
endmodule
