// Digital circuit add8bit.dig as structural Verilog
module add8bit (
  output B0,
  output A0
);

  add4bit add4bit_1 ();  // open: c0, S, ci, A, B
  add4bit add4bit_2 ();  // open: c0, S, ci, A, B
endmodule
