// Digital circuit add8bit2.dig as structural Verilog
module add8bit2 (
  input  [7:0] A,
  input  [7:0] B,
  input  ci,
  output [7:0] S,
  output C0
);

  wire add4bit2_0_2_c0;

  add4bit2_0 add4bit2_0_1 (.A(A[7:4]), .B(B[7:4]), .Ci(add4bit2_0_2_c0), .C0(C0), .S(S[7:4]));
  add4bit2_0 add4bit2_0_2 (.A(A[3:0]), .B(B[3:0]), .Ci(ci), .C0(add4bit2_0_2_c0), .S(S[3:0]));
endmodule
