// Digital circuit colaffich.dig as structural Verilog
module colaffich (
  input  in_1,
  input  in_2,
  input  in_3,
  input  [7:0] IN
);

  wire [7:0] registre8bit_1_out;

  LED led_1 (.in(registre8bit_1_out[6]));
  LED led_2 (.in(registre8bit_1_out[5]));
  LED led_3 (.in(registre8bit_1_out[4]));
  LED led_4 (.in(registre8bit_1_out[3]));
  LED led_5 (.in(registre8bit_1_out[2]));
  LED led_6 (.in(registre8bit_1_out[1]));
  LED led_7 (.in(registre8bit_1_out[0]));
  registre8bit registre8bit_1 (.in(IN), .CLK(in_1), .WE(in_2), .Reset(in_3), .out(registre8bit_1_out));

  // Other names for the same wires on the sheet: CLK = in_1; EN_AFF = in_2; RST_AFF = in_3
endmodule
