// Digital circuit colaffich32.dig as structural Verilog
module colaffich32 (
  input  [7:0] IN,
  input  in_2,
  input  in_3,
  input  in_4
);

  wire [7:0] registre8bit_1_out, registre8bit_2_out, registre8bit_3_out, registre8bit_4_out,
       registre8bit_5_out, registre8bit_6_out, registre8bit_7_out, registre8bit_8_out, registre8bit_9_out,
       registre8bit_10_out, registre8bit_12_out, registre8bit_13_out, registre8bit_14_out,
       registre8bit_15_out, registre8bit_16_out, registre8bit_17_out, registre8bit_18_out,
       registre8bit_20_out, registre8bit_21_out, registre8bit_22_out, registre8bit_23_out,
       registre8bit_24_out, registre8bit_25_out, registre8bit_26_out, registre8bit_28_out,
       registre8bit_29_out, registre8bit_30_out, registre8bit_31_out, registre8bit_32_out;

  registre8bit registre8bit_1 (.in(registre8bit_2_out), .CLK(in_2), .WE(in_3), .Reset(in_4), .out(registre8bit_1_out));
  registre8bit registre8bit_2 (.in(registre8bit_3_out), .CLK(in_2), .WE(in_3), .Reset(in_4), .out(registre8bit_2_out));
  registre8bit registre8bit_3 (.in(registre8bit_4_out), .CLK(in_2), .WE(in_3), .Reset(in_4), .out(registre8bit_3_out));
  LED led_1 (.in(registre8bit_1_out[6]));
  LED led_2 (.in(registre8bit_1_out[5]));
  LED led_3 (.in(registre8bit_1_out[4]));
  LED led_4 (.in(registre8bit_1_out[3]));
  LED led_5 (.in(registre8bit_1_out[2]));
  LED led_6 (.in(registre8bit_1_out[1]));
  LED led_7 (.in(registre8bit_1_out[0]));
  LED led_8 (.in(registre8bit_2_out[6]));
  LED led_9 (.in(registre8bit_2_out[5]));
  LED led_10 (.in(registre8bit_2_out[4]));
  LED led_11 (.in(registre8bit_2_out[3]));
  LED led_12 (.in(registre8bit_2_out[2]));
  LED led_13 (.in(registre8bit_2_out[1]));
  LED led_14 (.in(registre8bit_2_out[0]));
  registre8bit registre8bit_4 (.in(registre8bit_5_out), .CLK(in_2), .WE(in_3), .Reset(in_4), .out(registre8bit_4_out));
  LED led_15 (.in(registre8bit_3_out[6]));
  LED led_16 (.in(registre8bit_3_out[5]));
  LED led_17 (.in(registre8bit_3_out[4]));
  LED led_18 (.in(registre8bit_3_out[3]));
  LED led_19 (.in(registre8bit_3_out[2]));
  LED led_20 (.in(registre8bit_3_out[1]));
  LED led_21 (.in(registre8bit_3_out[0]));
  LED led_22 (.in(registre8bit_4_out[6]));
  LED led_23 (.in(registre8bit_4_out[5]));
  LED led_24 (.in(registre8bit_4_out[4]));
  LED led_25 (.in(registre8bit_4_out[3]));
  LED led_26 (.in(registre8bit_4_out[2]));
  LED led_27 (.in(registre8bit_4_out[1]));
  LED led_28 (.in(registre8bit_4_out[0]));
  LED led_29 (.in(registre8bit_5_out[6]));
  LED led_30 (.in(registre8bit_5_out[5]));
  LED led_31 (.in(registre8bit_5_out[4]));
  LED led_32 (.in(registre8bit_5_out[3]));
  LED led_33 (.in(registre8bit_5_out[2]));
  LED led_34 (.in(registre8bit_5_out[1]));
  LED led_35 (.in(registre8bit_5_out[0]));
  registre8bit registre8bit_5 (.in(registre8bit_6_out), .CLK(in_2), .WE(in_3), .Reset(in_4), .out(registre8bit_5_out));
  LED led_36 (.in(registre8bit_6_out[6]));
  LED led_37 (.in(registre8bit_6_out[5]));
  LED led_38 (.in(registre8bit_6_out[4]));
  LED led_39 (.in(registre8bit_6_out[3]));
  LED led_40 (.in(registre8bit_6_out[2]));
  LED led_41 (.in(registre8bit_6_out[1]));
  LED led_42 (.in(registre8bit_6_out[0]));
  LED led_43 (.in(registre8bit_8_out[6]));
  LED led_44 (.in(registre8bit_8_out[5]));
  LED led_45 (.in(registre8bit_8_out[4]));
  LED led_46 (.in(registre8bit_8_out[3]));
  LED led_47 (.in(registre8bit_8_out[2]));
  LED led_48 (.in(registre8bit_8_out[1]));
  LED led_49 (.in(registre8bit_8_out[0]));
  registre8bit registre8bit_6 (.in(registre8bit_8_out), .CLK(in_2), .WE(in_3), .Reset(in_4), .out(registre8bit_6_out));
  LED led_50 (.in(registre8bit_10_out[6]));
  LED led_51 (.in(registre8bit_10_out[5]));
  LED led_52 (.in(registre8bit_10_out[4]));
  LED led_53 (.in(registre8bit_10_out[3]));
  LED led_54 (.in(registre8bit_10_out[2]));
  LED led_55 (.in(registre8bit_10_out[1]));
  LED led_56 (.in(registre8bit_10_out[0]));
  registre8bit registre8bit_7 (.in(registre8bit_9_out), .CLK(in_2), .WE(in_3), .Reset(in_4), .out(registre8bit_7_out));
  registre8bit registre8bit_8 (.in(registre8bit_10_out), .CLK(in_2), .WE(in_3), .Reset(in_4), .out(registre8bit_8_out));
  LED led_57 (.in(registre8bit_7_out[6]));
  LED led_58 (.in(registre8bit_7_out[5]));
  LED led_59 (.in(registre8bit_7_out[4]));
  LED led_60 (.in(registre8bit_7_out[3]));
  LED led_61 (.in(registre8bit_7_out[2]));
  LED led_62 (.in(registre8bit_7_out[1]));
  LED led_63 (.in(registre8bit_7_out[0]));
  LED led_64 (.in(registre8bit_9_out[6]));
  LED led_65 (.in(registre8bit_9_out[5]));
  LED led_66 (.in(registre8bit_9_out[4]));
  LED led_67 (.in(registre8bit_9_out[3]));
  LED led_68 (.in(registre8bit_9_out[2]));
  LED led_69 (.in(registre8bit_9_out[1]));
  LED led_70 (.in(registre8bit_9_out[0]));
  registre8bit registre8bit_9 (.in(registre8bit_9_out), .CLK(in_2), .WE(in_3), .Reset(in_4), .out(registre8bit_9_out));
  registre8bit registre8bit_10 (
    .in(registre8bit_7_out), .CLK(in_2), .WE(in_3), .Reset(in_4), .out(registre8bit_10_out));
  LED led_71 (.in(registre8bit_9_out[6]));
  LED led_72 (.in(registre8bit_9_out[5]));
  LED led_73 (.in(registre8bit_9_out[4]));
  LED led_74 (.in(registre8bit_9_out[3]));
  LED led_75 (.in(registre8bit_9_out[2]));
  LED led_76 (.in(registre8bit_9_out[1]));
  LED led_77 (.in(registre8bit_9_out[0]));
  LED led_78 (.in(registre8bit_13_out[6]));
  LED led_79 (.in(registre8bit_13_out[5]));
  LED led_80 (.in(registre8bit_13_out[4]));
  LED led_81 (.in(registre8bit_13_out[3]));
  LED led_82 (.in(registre8bit_13_out[2]));
  LED led_83 (.in(registre8bit_13_out[1]));
  LED led_84 (.in(registre8bit_13_out[0]));
  registre8bit registre8bit_11 (
    .in(registre8bit_13_out), .CLK(in_2), .WE(in_3), .Reset(in_4), .out(registre8bit_9_out));
  LED led_85 (.in(registre8bit_16_out[6]));
  LED led_86 (.in(registre8bit_16_out[5]));
  LED led_87 (.in(registre8bit_16_out[4]));
  LED led_88 (.in(registre8bit_16_out[3]));
  LED led_89 (.in(registre8bit_16_out[2]));
  LED led_90 (.in(registre8bit_16_out[1]));
  LED led_91 (.in(registre8bit_16_out[0]));
  registre8bit registre8bit_12 (
    .in(registre8bit_14_out), .CLK(in_2), .WE(in_3), .Reset(in_4), .out(registre8bit_12_out));
  registre8bit registre8bit_13 (
    .in(registre8bit_16_out), .CLK(in_2), .WE(in_3), .Reset(in_4), .out(registre8bit_13_out));
  LED led_92 (.in(registre8bit_18_out[6]));
  LED led_93 (.in(registre8bit_18_out[5]));
  LED led_94 (.in(registre8bit_18_out[4]));
  LED led_95 (.in(registre8bit_18_out[3]));
  LED led_96 (.in(registre8bit_18_out[2]));
  LED led_97 (.in(registre8bit_18_out[1]));
  LED led_98 (.in(registre8bit_18_out[0]));
  LED led_99 (.in(registre8bit_14_out[6]));
  LED led_100 (.in(registre8bit_14_out[5]));
  LED led_101 (.in(registre8bit_14_out[4]));
  LED led_102 (.in(registre8bit_14_out[3]));
  LED led_103 (.in(registre8bit_14_out[2]));
  LED led_104 (.in(registre8bit_14_out[1]));
  LED led_105 (.in(registre8bit_14_out[0]));
  registre8bit registre8bit_14 (
    .in(registre8bit_15_out), .CLK(in_2), .WE(in_3), .Reset(in_4), .out(registre8bit_14_out));
  LED led_106 (.in(registre8bit_21_out[6]));
  LED led_107 (.in(registre8bit_21_out[5]));
  LED led_108 (.in(registre8bit_21_out[4]));
  LED led_109 (.in(registre8bit_21_out[3]));
  LED led_110 (.in(registre8bit_21_out[2]));
  LED led_111 (.in(registre8bit_21_out[1]));
  LED led_112 (.in(registre8bit_21_out[0]));
  registre8bit registre8bit_15 (
    .in(registre8bit_17_out), .CLK(in_2), .WE(in_3), .Reset(in_4), .out(registre8bit_15_out));
  registre8bit registre8bit_16 (
    .in(registre8bit_18_out), .CLK(in_2), .WE(in_3), .Reset(in_4), .out(registre8bit_16_out));
  LED led_113 (.in(registre8bit_12_out[6]));
  LED led_114 (.in(registre8bit_12_out[5]));
  LED led_115 (.in(registre8bit_12_out[4]));
  LED led_116 (.in(registre8bit_12_out[3]));
  LED led_117 (.in(registre8bit_12_out[2]));
  LED led_118 (.in(registre8bit_12_out[1]));
  LED led_119 (.in(registre8bit_12_out[0]));
  LED led_120 (.in(registre8bit_14_out[6]));
  LED led_121 (.in(registre8bit_14_out[5]));
  LED led_122 (.in(registre8bit_14_out[4]));
  LED led_123 (.in(registre8bit_14_out[3]));
  LED led_124 (.in(registre8bit_14_out[2]));
  LED led_125 (.in(registre8bit_14_out[1]));
  LED led_126 (.in(registre8bit_14_out[0]));
  registre8bit registre8bit_17 (
    .in(registre8bit_20_out), .CLK(in_2), .WE(in_3), .Reset(in_4), .out(registre8bit_17_out));
  registre8bit registre8bit_18 (
    .in(registre8bit_14_out), .CLK(in_2), .WE(in_3), .Reset(in_4), .out(registre8bit_18_out));
  LED led_127 (.in(registre8bit_15_out[6]));
  LED led_128 (.in(registre8bit_15_out[5]));
  LED led_129 (.in(registre8bit_15_out[4]));
  LED led_130 (.in(registre8bit_15_out[3]));
  LED led_131 (.in(registre8bit_15_out[2]));
  LED led_132 (.in(registre8bit_15_out[1]));
  LED led_133 (.in(registre8bit_15_out[0]));
  LED led_134 (.in(registre8bit_17_out[6]));
  LED led_135 (.in(registre8bit_17_out[5]));
  LED led_136 (.in(registre8bit_17_out[4]));
  LED led_137 (.in(registre8bit_17_out[3]));
  LED led_138 (.in(registre8bit_17_out[2]));
  LED led_139 (.in(registre8bit_17_out[1]));
  LED led_140 (.in(registre8bit_17_out[0]));
  registre8bit registre8bit_19 (
    .in(registre8bit_21_out), .CLK(in_2), .WE(in_3), .Reset(in_4), .out(registre8bit_14_out));
  LED led_141 (.in(registre8bit_20_out[6]));
  LED led_142 (.in(registre8bit_20_out[5]));
  LED led_143 (.in(registre8bit_20_out[4]));
  LED led_144 (.in(registre8bit_20_out[3]));
  LED led_145 (.in(registre8bit_20_out[2]));
  LED led_146 (.in(registre8bit_20_out[1]));
  LED led_147 (.in(registre8bit_20_out[0]));
  registre8bit registre8bit_20 (
    .in(registre8bit_22_out), .CLK(in_2), .WE(in_3), .Reset(in_4), .out(registre8bit_20_out));
  LED led_148 (.in(registre8bit_22_out[6]));
  LED led_149 (.in(registre8bit_22_out[5]));
  LED led_150 (.in(registre8bit_22_out[4]));
  LED led_151 (.in(registre8bit_22_out[3]));
  LED led_152 (.in(registre8bit_22_out[2]));
  LED led_153 (.in(registre8bit_22_out[1]));
  LED led_154 (.in(registre8bit_22_out[0]));
  registre8bit registre8bit_21 (
    .in(registre8bit_12_out), .CLK(in_2), .WE(in_3), .Reset(in_4), .out(registre8bit_21_out));
  LED led_155 (.in(registre8bit_24_out[6]));
  LED led_156 (.in(registre8bit_24_out[5]));
  LED led_157 (.in(registre8bit_24_out[4]));
  LED led_158 (.in(registre8bit_24_out[3]));
  LED led_159 (.in(registre8bit_24_out[2]));
  LED led_160 (.in(registre8bit_24_out[1]));
  LED led_161 (.in(registre8bit_24_out[0]));
  registre8bit registre8bit_22 (
    .in(registre8bit_24_out), .CLK(in_2), .WE(in_3), .Reset(in_4), .out(registre8bit_22_out));
  LED led_162 (.in(registre8bit_26_out[6]));
  LED led_163 (.in(registre8bit_26_out[5]));
  LED led_164 (.in(registre8bit_26_out[4]));
  LED led_165 (.in(registre8bit_26_out[3]));
  LED led_166 (.in(registre8bit_26_out[2]));
  LED led_167 (.in(registre8bit_26_out[1]));
  LED led_168 (.in(registre8bit_26_out[0]));
  registre8bit registre8bit_23 (
    .in(registre8bit_25_out), .CLK(in_2), .WE(in_3), .Reset(in_4), .out(registre8bit_23_out));
  registre8bit registre8bit_24 (
    .in(registre8bit_26_out), .CLK(in_2), .WE(in_3), .Reset(in_4), .out(registre8bit_24_out));
  LED led_169 (.in(registre8bit_23_out[6]));
  LED led_170 (.in(registre8bit_23_out[5]));
  LED led_171 (.in(registre8bit_23_out[4]));
  LED led_172 (.in(registre8bit_23_out[3]));
  LED led_173 (.in(registre8bit_23_out[2]));
  LED led_174 (.in(registre8bit_23_out[1]));
  LED led_175 (.in(registre8bit_23_out[0]));
  LED led_176 (.in(registre8bit_25_out[6]));
  LED led_177 (.in(registre8bit_25_out[5]));
  LED led_178 (.in(registre8bit_25_out[4]));
  LED led_179 (.in(registre8bit_25_out[3]));
  LED led_180 (.in(registre8bit_25_out[2]));
  LED led_181 (.in(registre8bit_25_out[1]));
  LED led_182 (.in(registre8bit_25_out[0]));
  registre8bit registre8bit_25 (
    .in(registre8bit_25_out), .CLK(in_2), .WE(in_3), .Reset(in_4), .out(registre8bit_25_out));
  registre8bit registre8bit_26 (
    .in(registre8bit_23_out), .CLK(in_2), .WE(in_3), .Reset(in_4), .out(registre8bit_26_out));
  LED led_183 (.in(registre8bit_25_out[6]));
  LED led_184 (.in(registre8bit_25_out[5]));
  LED led_185 (.in(registre8bit_25_out[4]));
  LED led_186 (.in(registre8bit_25_out[3]));
  LED led_187 (.in(registre8bit_25_out[2]));
  LED led_188 (.in(registre8bit_25_out[1]));
  LED led_189 (.in(registre8bit_25_out[0]));
  LED led_190 (.in(registre8bit_28_out[6]));
  LED led_191 (.in(registre8bit_28_out[5]));
  LED led_192 (.in(registre8bit_28_out[4]));
  LED led_193 (.in(registre8bit_28_out[3]));
  LED led_194 (.in(registre8bit_28_out[2]));
  LED led_195 (.in(registre8bit_28_out[1]));
  LED led_196 (.in(registre8bit_28_out[0]));
  registre8bit registre8bit_27 (
    .in(registre8bit_28_out), .CLK(in_2), .WE(in_3), .Reset(in_4), .out(registre8bit_25_out));
  LED led_197 (.in(registre8bit_29_out[6]));
  LED led_198 (.in(registre8bit_29_out[5]));
  LED led_199 (.in(registre8bit_29_out[4]));
  LED led_200 (.in(registre8bit_29_out[3]));
  LED led_201 (.in(registre8bit_29_out[2]));
  LED led_202 (.in(registre8bit_29_out[1]));
  LED led_203 (.in(registre8bit_29_out[0]));
  registre8bit registre8bit_28 (
    .in(registre8bit_29_out), .CLK(in_2), .WE(in_3), .Reset(in_4), .out(registre8bit_28_out));
  LED led_204 (.in(registre8bit_30_out[6]));
  LED led_205 (.in(registre8bit_30_out[5]));
  LED led_206 (.in(registre8bit_30_out[4]));
  LED led_207 (.in(registre8bit_30_out[3]));
  LED led_208 (.in(registre8bit_30_out[2]));
  LED led_209 (.in(registre8bit_30_out[1]));
  LED led_210 (.in(registre8bit_30_out[0]));
  LED led_211 (.in(registre8bit_31_out[6]));
  LED led_212 (.in(registre8bit_31_out[5]));
  LED led_213 (.in(registre8bit_31_out[4]));
  LED led_214 (.in(registre8bit_31_out[3]));
  LED led_215 (.in(registre8bit_31_out[2]));
  LED led_216 (.in(registre8bit_31_out[1]));
  LED led_217 (.in(registre8bit_31_out[0]));
  LED led_218 (.in(registre8bit_32_out[6]));
  LED led_219 (.in(registre8bit_32_out[5]));
  LED led_220 (.in(registre8bit_32_out[4]));
  LED led_221 (.in(registre8bit_32_out[3]));
  LED led_222 (.in(registre8bit_32_out[2]));
  LED led_223 (.in(registre8bit_32_out[1]));
  LED led_224 (.in(registre8bit_32_out[0]));
  registre8bit registre8bit_29 (
    .in(registre8bit_30_out), .CLK(in_2), .WE(in_3), .Reset(in_4), .out(registre8bit_29_out));
  registre8bit registre8bit_30 (
    .in(registre8bit_31_out), .CLK(in_2), .WE(in_3), .Reset(in_4), .out(registre8bit_30_out));
  registre8bit registre8bit_31 (
    .in(registre8bit_32_out), .CLK(in_2), .WE(in_3), .Reset(in_4), .out(registre8bit_31_out));
  registre8bit registre8bit_32 (.in(IN), .CLK(in_2), .WE(in_3), .Reset(in_4), .out(registre8bit_32_out));

  // Other names for the same wires on the sheet: CLK = in_2; EN_AFF = in_3; RST_AFF = in_4
endmodule
