// Digital circuit colaffich8.dig as structural Verilog
module colaffich8 (
  input  [7:0] IN,
  input  in_2,
  input  in_3,
  input  in_4
);

  wire [7:0] registre8bit_1_out, registre8bit_2_out, registre8bit_3_out, registre8bit_4_out,
       registre8bit_5_out, registre8bit_6_out, registre8bit_7_out, registre8bit_8_out;

  registre8bit registre8bit_1 (.in(registre8bit_2_out), .CLK(in_2), .WE(in_3), .Reset(in_4), .out(registre8bit_1_out));
  registre8bit registre8bit_2 (.in(registre8bit_3_out), .CLK(in_2), .WE(in_3), .Reset(in_4), .out(registre8bit_2_out));
  registre8bit registre8bit_3 (.in(registre8bit_4_out), .CLK(in_2), .WE(in_3), .Reset(in_4), .out(registre8bit_3_out));
  LED led_1 (.in(registre8bit_1_out[6]));
  LED led_2 (.in(registre8bit_1_out[5]));
  LED led_3 (.in(registre8bit_1_out[4]));
  LED led_4 (.in(registre8bit_1_out[3]));
  LED led_5 (.in(registre8bit_1_out[2]));
  LED led_6 (.in(registre8bit_1_out[1]));
  LED led_7 (.in(registre8bit_1_out[0]));
  LED led_8 (.in(registre8bit_2_out[6]));
  LED led_9 (.in(registre8bit_2_out[5]));
  LED led_10 (.in(registre8bit_2_out[4]));
  LED led_11 (.in(registre8bit_2_out[3]));
  LED led_12 (.in(registre8bit_2_out[2]));
  LED led_13 (.in(registre8bit_2_out[1]));
  LED led_14 (.in(registre8bit_2_out[0]));
  registre8bit registre8bit_4 (.in(registre8bit_5_out), .CLK(in_2), .WE(in_3), .Reset(in_4), .out(registre8bit_4_out));
  LED led_15 (.in(registre8bit_3_out[6]));
  LED led_16 (.in(registre8bit_3_out[5]));
  LED led_17 (.in(registre8bit_3_out[4]));
  LED led_18 (.in(registre8bit_3_out[3]));
  LED led_19 (.in(registre8bit_3_out[2]));
  LED led_20 (.in(registre8bit_3_out[1]));
  LED led_21 (.in(registre8bit_3_out[0]));
  LED led_22 (.in(registre8bit_4_out[6]));
  LED led_23 (.in(registre8bit_4_out[5]));
  LED led_24 (.in(registre8bit_4_out[4]));
  LED led_25 (.in(registre8bit_4_out[3]));
  LED led_26 (.in(registre8bit_4_out[2]));
  LED led_27 (.in(registre8bit_4_out[1]));
  LED led_28 (.in(registre8bit_4_out[0]));
  LED led_29 (.in(registre8bit_5_out[6]));
  LED led_30 (.in(registre8bit_5_out[5]));
  LED led_31 (.in(registre8bit_5_out[4]));
  LED led_32 (.in(registre8bit_5_out[3]));
  LED led_33 (.in(registre8bit_5_out[2]));
  LED led_34 (.in(registre8bit_5_out[1]));
  LED led_35 (.in(registre8bit_5_out[0]));
  registre8bit registre8bit_5 (.in(registre8bit_6_out), .CLK(in_2), .WE(in_3), .Reset(in_4), .out(registre8bit_5_out));
  LED led_36 (.in(registre8bit_6_out[6]));
  LED led_37 (.in(registre8bit_6_out[5]));
  LED led_38 (.in(registre8bit_6_out[4]));
  LED led_39 (.in(registre8bit_6_out[3]));
  LED led_40 (.in(registre8bit_6_out[2]));
  LED led_41 (.in(registre8bit_6_out[1]));
  LED led_42 (.in(registre8bit_6_out[0]));
  LED led_43 (.in(registre8bit_7_out[6]));
  LED led_44 (.in(registre8bit_7_out[5]));
  LED led_45 (.in(registre8bit_7_out[4]));
  LED led_46 (.in(registre8bit_7_out[3]));
  LED led_47 (.in(registre8bit_7_out[2]));
  LED led_48 (.in(registre8bit_7_out[1]));
  LED led_49 (.in(registre8bit_7_out[0]));
  registre8bit registre8bit_6 (.in(registre8bit_7_out), .CLK(in_2), .WE(in_3), .Reset(in_4), .out(registre8bit_6_out));
  LED led_50 (.in(registre8bit_8_out[6]));
  LED led_51 (.in(registre8bit_8_out[5]));
  LED led_52 (.in(registre8bit_8_out[4]));
  LED led_53 (.in(registre8bit_8_out[3]));
  LED led_54 (.in(registre8bit_8_out[2]));
  LED led_55 (.in(registre8bit_8_out[1]));
  LED led_56 (.in(registre8bit_8_out[0]));
  registre8bit registre8bit_7 (.in(registre8bit_8_out), .CLK(in_2), .WE(in_3), .Reset(in_4), .out(registre8bit_7_out));
  registre8bit registre8bit_8 (.in(IN), .CLK(in_2), .WE(in_3), .Reset(in_4), .out(registre8bit_8_out));

  // Other names for the same wires on the sheet: CLK = in_2; EN_AFF = in_3; RST_AFF = in_4
endmodule
