// Digital circuit comp1bit.dig as structural Verilog
module comp1bit (
  input  A,
  input  B,
  output Cmp
);

  wire and_1_out, and_2_out, not_1_out, not_2_out;

  and and_1 (and_1_out, A, B);
  not not_1 (not_1_out, A);
  not not_2 (not_2_out, B);
  and and_2 (and_2_out, not_1_out, not_2_out);
  or or_1 (Cmp, and_1_out, and_2_out);
endmodule
