// Digital circuit comp8bit.dig as structural Verilog
module comp8bit (
  input  [7:0] A,
  input  [7:0] B,
  output out
);

  wire comp1bit_1_cmp, comp1bit_2_cmp, comp1bit_3_cmp, comp1bit_4_cmp, comp1bit_5_cmp, comp1bit_6_cmp,
       comp1bit_7_cmp, comp1bit_8_cmp;

  comp1bit comp1bit_1 (.A(A[0]), .B(B[0]), .Cmp(comp1bit_1_cmp));
  comp1bit comp1bit_2 (.A(A[1]), .B(B[1]), .Cmp(comp1bit_2_cmp));
  comp1bit comp1bit_3 (.A(A[2]), .B(B[2]), .Cmp(comp1bit_3_cmp));
  comp1bit comp1bit_4 (.A(A[3]), .B(B[3]), .Cmp(comp1bit_4_cmp));
  comp1bit comp1bit_5 (.A(A[4]), .B(B[4]), .Cmp(comp1bit_5_cmp));
  comp1bit comp1bit_6 (.A(A[5]), .B(B[5]), .Cmp(comp1bit_6_cmp));
  comp1bit comp1bit_7 (.A(A[6]), .B(B[6]), .Cmp(comp1bit_7_cmp));
  comp1bit comp1bit_8 (.A(A[7]), .B(B[7]), .Cmp(comp1bit_8_cmp));
  and and_1 (out, comp1bit_1_cmp, comp1bit_2_cmp, comp1bit_3_cmp, comp1bit_4_cmp, comp1bit_5_cmp, comp1bit_6_cmp, comp1bit_7_cmp, comp1bit_8_cmp);
endmodule
