// Digital circuit registre8bit.dig as structural Verilog
module registre8bit (
  input  [7:0] in,
  input  CLK,
  input  WE,
  input  Reset,
  output [7:0] out
);

  D_fliflop_res1bit d_fliflop_res1bit_1 (.D(in[0]), .EN(WE), .CLK(CLK), .Reset(Reset), .Q(out[0]));
  D_fliflop_res1bit d_fliflop_res1bit_2 (.D(in[1]), .EN(WE), .CLK(CLK), .Reset(Reset), .Q(out[1]));
  D_fliflop_res1bit d_fliflop_res1bit_3 (.D(in[2]), .EN(WE), .CLK(CLK), .Reset(Reset), .Q(out[2]));
  D_fliflop_res1bit d_fliflop_res1bit_4 (.D(in[3]), .EN(WE), .CLK(CLK), .Reset(Reset), .Q(out[3]));
  D_fliflop_res1bit d_fliflop_res1bit_5 (.D(in[4]), .EN(WE), .CLK(CLK), .Reset(Reset), .Q(out[4]));
  D_fliflop_res1bit d_fliflop_res1bit_6 (.D(in[5]), .EN(WE), .CLK(CLK), .Reset(Reset), .Q(out[5]));
  D_fliflop_res1bit d_fliflop_res1bit_7 (.D(in[6]), .EN(WE), .CLK(CLK), .Reset(Reset), .Q(out[6]));
  D_fliflop_res1bit d_fliflop_res1bit_8 (.D(in[7]), .EN(WE), .CLK(CLK), .Reset(Reset), .Q(out[7]));
endmodule
